// Logisim project Design_Project_1.circ as structural Verilog: 1 circuit, main circuit main
module main (
  input  in_1,
  input  D21,
  input  in_3,
  input  D22,
  input  D23,
  input  in_6,
  input  D24,
  input  D25,
  input  in_9,
  input  D26,
  input  D27,
  input  in_12,
  input  D28,
  input  D29,
  input  in_15,
  input  D30,
  input  D31,
  input  in_18,
  input  in_19,
  input  in_20,
  input  in_21,
  input  in_22,
  input  in_23,
  input  in_24,
  input  in_25,
  input  in_26,
  input  in_27
);

  wire and_1_out, and_2_out, decoder_1_out0, decoder_1_out1, decoder_1_out2, decoder_1_out3, decoder_1_out4,
       decoder_1_out5, decoder_1_out6, decoder_1_out7, decoder_1_out8, decoder_1_out9, decoder_1_out10,
       decoder_1_out11, decoder_1_out12, decoder_1_out13, decoder_1_out14, decoder_1_out15, not_1_out,
       or_1_out, P0_out, P1_out, P2_out, P3_out, P4_out, xor_1_out, xor_2_out, xor_3_out, xor_4_out,
       xor_5_out, xor_6_out, xor_7_out, xor_8_out, xor_9_out, xor_10_out, xor_11_out, xor_12_out, xor_13_out,
       xor_14_out, xor_15_out, xor_16_out, xor_17_out, xor_18_out, xor_19_out, xor_20_out, xor_21_out,
       xor_22_out, xor_23_out, xor_24_out, xor_25_out, xor_26_out, xor_27_out, xor_28_out, xor_29_out,
       xor_30_out, xor_31_out, xor_32_out, xor_33_out, xor_34_out, xor_35_out, xor_36_out, xor_37_out,
       xor_38_out, xor_39_out, xor_40_out, xor_41_out, xor_42_out, xor_43_out, xor_44_out, xor_45_out,
       xor_46_out, xor_47_out, xor_48_out, xor_49_out, xor_50_out, xor_51_out, xor_52_out, xor_53_out,
       xor_54_out, xor_55_out, xor_56_out, xor_57_out, xor_58_out, xor_59_out, xor_60_out, xor_61_out,
       xor_62_out, xor_63_out, xor_64_out, xor_65_out, xor_66_out, xor_67_out, xor_68_out, xor_69_out,
       xor_70_out, xor_71_out, xor_72_out, xor_73_out, xor_74_out, xor_75_out, xor_76_out, xor_77_out,
       xor_78_out, xor_79_out, xor_80_out, xor_81_out, xor_82_out, xor_85_out, xor_88_out, xor_89_out,
       xor_90_out, xor_91_out, xor_103_out, xor_104_out, xor_105_out, xor_106_out, xor_107_out;
  wire [3:0] xor_83_out;

  xor xor_1 (xor_1_out, D21, D22);
  xor xor_2 (xor_2_out, D23, D24);
  xor xor_3 (xor_3_out, D25, D26);
  xor xor_4 (xor_4_out, D27, D28);
  xor xor_5 (xor_5_out, D29, D30);
  xor xor_6 (xor_6_out, D21, D22);
  xor xor_7 (xor_7_out, D24, D25);
  xor xor_8 (xor_8_out, D27, D29);
  xor xor_9 (xor_9_out, D21, D23);
  xor xor_10 (xor_10_out, D24, D26);
  xor xor_11 (xor_11_out, D27, D30);
  xor xor_12 (xor_12_out, D22, D23);
  xor xor_13 (xor_13_out, D24, D28);
  xor xor_14 (xor_14_out, D29, D30);
  xor xor_15 (xor_15_out, xor_5_out, D31);
  xor xor_16 (xor_16_out, D25, D26);
  xor xor_17 (xor_17_out, D27, D28);
  buf xor_18 (xor_18_out, D29);  // XOR_Gate
  xor xor_19 (xor_19_out, xor_1_out, xor_2_out);
  xor xor_20 (xor_20_out, xor_3_out, xor_4_out);
  xor xor_21 (xor_21_out, xor_9_out, xor_10_out);
  xor xor_22 (xor_22_out, xor_11_out, D31);
  xor xor_23 (xor_23_out, xor_12_out, xor_13_out);
  xor xor_24 (xor_24_out, xor_14_out, D31);
  xor xor_25 (xor_25_out, xor_19_out, xor_20_out);
  xor xor_26 (xor_26_out, xor_6_out, xor_7_out);
  xor xor_27 (xor_27_out, xor_8_out, D31);
  xor xor_28 (xor_28_out, xor_16_out, xor_17_out);
  xor xor_29 (xor_29_out, xor_18_out, D31);
  xor P1 (P1_out, xor_26_out, xor_27_out);
  xor P2 (P2_out, xor_21_out, xor_22_out);
  xor P3 (P3_out, xor_23_out, xor_24_out);
  xor P4 (P4_out, xor_28_out, xor_29_out);
  xor xor_30 (xor_30_out, xor_25_out, xor_15_out);
  LED led_1 (.in(P1_out));
  LED led_2 (.in(P2_out));
  LED led_3 (.in(P3_out));
  LED led_4 (.in(P4_out));
  xor xor_31 (xor_31_out, P1_out, P2_out);
  xor xor_32 (xor_32_out, P3_out, P4_out);
  xor xor_33 (xor_33_out, xor_31_out, xor_32_out);
  xor P0 (P0_out, xor_30_out, xor_33_out);
  LED led_5 (.in(P0_out));
  xor xor_34 (xor_34_out, D21, in_1);
  xor xor_35 (xor_35_out, D22, in_3);
  xor xor_36 (xor_36_out, D23, in_6);
  xor xor_37 (xor_37_out, D24, in_9);
  xor xor_38 (xor_38_out, D25, in_12);
  xor xor_39 (xor_39_out, D26, in_15);
  xor xor_40 (xor_40_out, D27, in_18);
  xor xor_41 (xor_41_out, D28, in_19);
  xor xor_42 (xor_42_out, D29, in_20);
  xor xor_43 (xor_43_out, D30, in_21);
  xor xor_44 (xor_44_out, D31, in_22);
  xor xor_45 (xor_45_out, P1_out, in_23);
  xor xor_46 (xor_46_out, P2_out, in_24);
  xor xor_47 (xor_47_out, P3_out, in_25);
  xor xor_48 (xor_48_out, P4_out, in_26);
  xor xor_49 (xor_49_out, P0_out, in_27);
  xor xor_50 (xor_50_out, xor_34_out, xor_35_out);
  xor xor_51 (xor_51_out, xor_37_out, xor_38_out);
  xor xor_52 (xor_52_out, xor_40_out, xor_42_out);
  xor xor_53 (xor_53_out, xor_34_out, xor_36_out);
  xor xor_54 (xor_54_out, xor_37_out, xor_39_out);
  xor xor_55 (xor_55_out, xor_40_out, xor_43_out);
  xor xor_56 (xor_56_out, xor_35_out, xor_36_out);
  xor xor_57 (xor_57_out, xor_37_out, xor_41_out);
  xor xor_58 (xor_58_out, xor_42_out, xor_43_out);
  xor xor_59 (xor_59_out, xor_38_out, xor_39_out);
  xor xor_60 (xor_60_out, xor_40_out, xor_41_out);
  xor xor_61 (xor_61_out, xor_42_out, xor_43_out);
  xor xor_62 (xor_62_out, xor_34_out, xor_35_out);
  xor xor_63 (xor_63_out, xor_36_out, xor_37_out);
  xor xor_64 (xor_64_out, xor_38_out, xor_39_out);
  xor xor_65 (xor_65_out, xor_40_out, xor_41_out);
  xor xor_66 (xor_66_out, xor_42_out, xor_43_out);
  xor xor_67 (xor_67_out, xor_66_out, xor_44_out);
  xor xor_68 (xor_68_out, xor_50_out, xor_51_out);
  xor xor_69 (xor_69_out, xor_52_out, xor_44_out);
  xor xor_70 (xor_70_out, xor_53_out, xor_54_out);
  xor xor_71 (xor_71_out, xor_55_out, xor_44_out);
  xor xor_72 (xor_72_out, xor_56_out, xor_57_out);
  xor xor_73 (xor_73_out, xor_58_out, xor_44_out);
  xor xor_74 (xor_74_out, xor_59_out, xor_60_out);
  xor xor_75 (xor_75_out, xor_61_out, xor_44_out);
  xor xor_76 (xor_76_out, xor_62_out, xor_63_out);
  xor xor_77 (xor_77_out, xor_64_out, xor_65_out);
  xor xor_78 (xor_78_out, xor_76_out, xor_77_out);
  xor xor_79 (xor_79_out, xor_68_out, xor_69_out);
  xor xor_80 (xor_80_out, xor_70_out, xor_71_out);
  xor xor_81 (xor_81_out, xor_72_out, xor_73_out);
  xor xor_82 (xor_82_out, xor_78_out, xor_67_out);
  xor xor_83 (xor_83_out[0], xor_79_out, xor_45_out);
  xor xor_84 (xor_83_out[1], xor_80_out, xor_46_out);
  xor xor_85 (xor_85_out, xor_74_out, xor_75_out);
  LED led_6 (.in(xor_83_out[1]));
  xor xor_86 (xor_83_out[2], xor_81_out, xor_47_out);
  LED led_7 (.in(xor_85_out));
  LED led_8 (.in(xor_83_out[2]));
  xor xor_87 (xor_83_out[3], xor_85_out, xor_48_out);
  LED led_9 (.in(xor_83_out[0]));
  xor xor_88 (xor_88_out, xor_83_out[0], xor_83_out[1]);
  xor xor_89 (xor_89_out, xor_83_out[2], xor_85_out);
  Decoder #(.enable("false"), .select(4)) decoder_1 (
    .out0(decoder_1_out0), .out1(decoder_1_out1), .out2(decoder_1_out2), .out3(decoder_1_out3),
    .out4(decoder_1_out4), .out5(decoder_1_out5), .out6(decoder_1_out6), .out7(decoder_1_out7),
    .out8(decoder_1_out8), .out9(decoder_1_out9), .out10(decoder_1_out10), .out11(decoder_1_out11),
    .out12(decoder_1_out12), .out13(decoder_1_out13), .out14(decoder_1_out14), .out15(decoder_1_out15),
    .sel(xor_83_out));
  xor xor_90 (xor_90_out, xor_88_out, xor_89_out);
  xor xor_91 (xor_91_out, xor_90_out, xor_82_out);
  // XOR_Gate xor_92 has open pins: in0=xor_34_out, in1=decoder_1_out3, out=open
  // XOR_Gate xor_93 has open pins: in0=xor_35_out, in1=decoder_1_out5, out=open
  // XOR_Gate xor_94 has open pins: in0=xor_36_out, in1=decoder_1_out6, out=open
  // XOR_Gate xor_95 has open pins: in0=xor_37_out, in1=decoder_1_out7, out=open
  // XOR_Gate xor_96 has open pins: in0=xor_38_out, in1=decoder_1_out9, out=open
  // XOR_Gate xor_97 has open pins: in0=xor_39_out, in1=decoder_1_out10, out=open
  // XOR_Gate xor_98 has open pins: in0=decoder_1_out11, in1=xor_40_out, out=open
  // XOR_Gate xor_99 has open pins: in0=decoder_1_out12, in1=xor_41_out, out=open
  // XOR_Gate xor_100 has open pins: in0=decoder_1_out13, in1=xor_42_out, out=open
  // XOR_Gate xor_101 has open pins: in0=decoder_1_out14, in1=xor_43_out, out=open
  // XOR_Gate xor_102 has open pins: in0=decoder_1_out15, in1=xor_44_out, out=open
  xor xor_103 (xor_103_out, decoder_1_out1, P1_out);
  xor xor_104 (xor_104_out, decoder_1_out2, P2_out);
  xor xor_105 (xor_105_out, decoder_1_out4, P3_out);
  xor xor_106 (xor_106_out, decoder_1_out8, P4_out);
  xor xor_107 (xor_107_out, P0_out, xor_91_out);
  or or_1 (or_1_out, xor_103_out, xor_104_out, xor_105_out, xor_106_out);
  LED led_10 (.in(decoder_1_out0));
  LED led_11 (.in(and_1_out));
  and and_1 (and_1_out, or_1_out, xor_107_out);
  LED led_12 (.in(and_2_out));
  and and_2 (and_2_out, or_1_out, not_1_out);
  not not_1 (not_1_out, xor_107_out);

  // Notes on the sheet:
  //   ENCODER
  //   PARITY 0
  //   PARITY 1
  //   PARITY 2
  //   PARITY 3
  //   PARITY 4
  //   NOISE
  //   N_D1
  //   N_D2
  //   N_D3
  //   N_D4
  //   N_D5
  //   N_D6
  //   N_D7
  //   N_D8
  //   N_D9
  //   N_D10
  //   N_D11
  //   N_P1
  //   N_P2
  //   N_P3
  //   N_P4
  //   N_P0
  //   Parity 1 OUT
  //   Parity 2 OUT
  //   Parity 3 OUT
  //   Parity 4 OUT
  //   PARITY 0
  //   P1 OUT
  //   P2 OUT
  //   P3 OUT
  //   P4 OUT
  //   P0
  //   DECODER
  //   D_D1
  //   D_D2
  //   D_D3
  //   D_D4
  //   D_D5
  //   D_D6
  //   D_D7
  //   D_D8
  //   D_D9
  //   D_D10
  //   D_D11
  //   P1
  //   P2
  //   P3
  //   P4
  //   P0
  //   No  Error
  //   One Bit Error
  //   Two Bit Error
endmodule
